# Fritzing sketch Final Harmonizing (saved by Fritzing 0.9.3b)
circuit board: 5.50611cm x 1.94544cm
circuit board: 10cm x 6cm
circuit board: 5.56255cm x 4.29444cm
breadboards: 1

parts:
  +_-_CS_RE_DC_OS_SC_BL_IS = female pin header, 9 pins [form="♀ (female)"]
  + = Pushbutton [package="[THT]"]
  +_2 = Pushbutton [package="[THT]"]
  +_3 = Pushbutton [package="[THT]"]
  R2 = Resistor [tolerance=±5% resistance=10k package=THT]
  R3 = Resistor [tolerance=±5% resistance=10k package=THT]
  R4 = Resistor [tolerance=±5% resistance=10k package=THT]
  -_+_G_O_AR = female pin header, 5 pins [form="♀ (female)"]
  ProMini = Arduino Pro Mini (3.3V)
  +_- = female pin header, 2 pins [form="♀ (female)"]
  RX_TX_+_- = female pin header, 4 pins [form="♀ (female)"]
  HB = female pin header, 2 pins [form="♀ (female)"]
  10K = Resistor [tolerance=±5% resistance=10k package=THT]
  R_C_L_-_+ = female pin header, 5 pins [form="♀ (female)"]
  R_C_L_-_+_2 = female pin header, 5 pins [form="♀ (female)"]
  I/O = female pin header, 3 pins [form="♀ (female)"]
  POT = female pin header, 5 pins [form="♀ (female)"]

nets (from the pcb view):
  N1: +_-_CS_RE_DC_OS_SC_BL_IS.pin1, +_-_CS_RE_DC_OS_SC_BL_IS.pin8, -_+_G_O_AR.pin4, ProMini.VCC, RX_TX_+_-.pin2, 10K.Pin_0, R_C_L_-_+.pin1, I/O.pin1, POT.pin2
  N2: +_-_CS_RE_DC_OS_SC_BL_IS.pin2, -_+_G_O_AR.pin3, -_+_G_O_AR.pin5, ProMini.GND, +_-.pin2, RX_TX_+_-.pin1, HB.pin2, R_C_L_-_+.pin2, POT.pin1, POT.pin4, POT.pin5
  N3: +_-_CS_RE_DC_OS_SC_BL_IS.pin3, ProMini.D10
  N4: +_-_CS_RE_DC_OS_SC_BL_IS.pin4, ProMini.D9
  N5: +_-_CS_RE_DC_OS_SC_BL_IS.pin5, ProMini.D8
  N6: +_-_CS_RE_DC_OS_SC_BL_IS.pin6, ProMini.MOSI
  N7: +_-_CS_RE_DC_OS_SC_BL_IS.pin7, ProMini.SCK
  N8: +_-_CS_RE_DC_OS_SC_BL_IS.pin9, ProMini.MISO
  N9: +.Pin_1, +.Pin_2, R2.Pin_0, R_C_L_-_+_2.pin3
  N10: +.Pin_3, +.Pin_4, +_2.Pin_1, +_2.Pin_2, +_3.Pin_3, +_3.Pin_4, R_C_L_-_+_2.pin2
  N11: +_2.Pin_3, +_2.Pin_4, R3.Pin_1, R_C_L_-_+_2.pin5
  N12: +_3.Pin_1, +_3.Pin_2, R4.Pin_0, R_C_L_-_+_2.pin4
  N13: R2.Pin_1, R3.Pin_0, R4.Pin_1, R_C_L_-_+_2.pin1
  N14: -_+_G_O_AR.pin2, ProMini.A0
  N15: ProMini.A1, POT.pin3
  N16: ProMini.D7, RX_TX_+_-.pin4
  N17: ProMini.D6, RX_TX_+_-.pin3
  N18: ProMini.D5, R_C_L_-_+.pin5
  N19: ProMini.D4, R_C_L_-_+.pin4
  N20: ProMini.D3, R_C_L_-_+.pin3
  N21: ProMini.D2, HB.pin1, 10K.Pin_1
  N22: +_-.pin1, I/O.pin2
